// Logisim project final-project-combinational.circ as structural Verilog: 1 circuit, main circuit main
module main (
  input  [2:0] in_1
);

  wire decoder_1_out0, decoder_1_out1, decoder_1_out2, decoder_1_out3, decoder_1_out4, decoder_1_out5,
       decoder_1_out6, decoder_1_out7, or_1_out, or_2_out, or_3_out, or_4_out, or_5_out, or_6_out, or_7_out,
       or_8_out, or_9_out, or_10_out, or_11_out, or_12_out, or_13_out;

  Decoder #(.select(3)) decoder_1 (
    .out0(decoder_1_out0), .out1(decoder_1_out1), .out2(decoder_1_out2), .out3(decoder_1_out3),
    .out4(decoder_1_out4), .out5(decoder_1_out5), .out6(decoder_1_out6), .out7(decoder_1_out7), .sel(in_1));  // open: en
  or or_1 (or_1_out, decoder_1_out0, decoder_1_out1, decoder_1_out2);
  or or_2 (or_2_out, decoder_1_out4, decoder_1_out3, decoder_1_out7);
  or or_3 (or_3_out, decoder_1_out3, decoder_1_out4, decoder_1_out5);
  or or_4 (or_4_out, decoder_1_out1, decoder_1_out4, decoder_1_out7, decoder_1_out5);
  or or_5 (or_5_out, decoder_1_out0, decoder_1_out1, decoder_1_out2);
  or or_6 (or_6_out, decoder_1_out3, decoder_1_out7, decoder_1_out4);
  or or_7 (or_7_out, decoder_1_out0, decoder_1_out2, decoder_1_out7, decoder_1_out3);
  or or_8 (or_8_out, decoder_1_out0, decoder_1_out1, decoder_1_out2, decoder_1_out7);
  or or_9 (or_9_out, decoder_1_out1, decoder_1_out2, decoder_1_out3);
  or or_10 (or_10_out, decoder_1_out4, decoder_1_out7, decoder_1_out6);
  or or_11 (or_11_out, or_1_out, or_2_out);
  or or_12 (or_12_out, or_5_out, or_6_out);
  or or_13 (or_13_out, or_9_out, or_10_out);
  _7_Segment_Display u_7_segment_display_1 (
    .g(or_13_out), .f(or_8_out), .a(or_11_out), .b(or_3_out), .e(or_7_out), .d(or_12_out), .c(or_4_out));  // open: dp

  // Notes on the sheet:
  //   B
  //   C
  //   E
  //   F
  //   A
  //   D
  //   G
endmodule
