// Logisim project final-projectsequential-updated.circ as structural Verilog: 1 circuit, main circuit main
module main (
);

  wire A, and_1_out, and_2_out, and_3_out, and_4_out, and_5_out, and_6_out, and_7_out, and_8_out, B, C,
       clock_1_out, decoder_1_out0, decoder_1_out1, decoder_1_out2, decoder_1_out3, decoder_1_out4,
       decoder_1_out5, decoder_1_out6, decoder_1_out7, or_1_out, or_2_out, or_3_out, or_4_out, or_5_out,
       or_6_out, or_7_out, or_8_out, or_9_out, or_10_out, or_11_out, or_12_out, or_13_out, or_14_out,
       or_15_out, or_16_out, or_17_out, or_18_out, W, W_prime, X_prime, Y_prime, Z_prime;

  Decoder #(.select(3)) decoder_1 (
    .out0(decoder_1_out0), .out1(decoder_1_out1), .out2(decoder_1_out2), .out3(decoder_1_out3),
    .out4(decoder_1_out4), .out5(decoder_1_out5), .out6(decoder_1_out6), .out7(decoder_1_out7),
    .sel({A, B, C}));  // open: en
  or or_1 (or_1_out, decoder_1_out0, decoder_1_out1, decoder_1_out2);
  or or_2 (or_2_out, decoder_1_out4, decoder_1_out3, decoder_1_out7);
  or or_3 (or_3_out, decoder_1_out3, decoder_1_out4, decoder_1_out5);
  or or_4 (or_4_out, decoder_1_out1, decoder_1_out4, decoder_1_out7, decoder_1_out5);
  or or_5 (or_5_out, decoder_1_out0, decoder_1_out1, decoder_1_out2);
  or or_6 (or_6_out, decoder_1_out3, decoder_1_out7, decoder_1_out4);
  or or_7 (or_7_out, decoder_1_out0, decoder_1_out2, decoder_1_out7, decoder_1_out3);
  or or_8 (or_8_out, decoder_1_out0, decoder_1_out1, decoder_1_out2, decoder_1_out7);
  or or_9 (or_9_out, decoder_1_out1, decoder_1_out2, decoder_1_out3);
  or or_10 (or_10_out, decoder_1_out4, decoder_1_out7, decoder_1_out6);
  or or_11 (or_11_out, or_1_out, or_2_out);
  or or_12 (or_12_out, or_5_out, or_6_out);
  or or_13 (or_13_out, or_9_out, or_10_out);
  _7_Segment_Display u_7_segment_display_1 (
    .g(or_13_out), .f(or_8_out), .a(or_11_out), .b(or_3_out), .e(or_7_out), .d(or_12_out), .c(or_4_out));  // open: dp
  Clock clock_1 (.out(clock_1_out));
  and and_1 (and_1_out, W_prime, A);
  and and_2 (and_2_out, B, C);
  and and_3 (and_3_out, W, Y_prime);
  and and_4 (and_4_out, A, Y_prime);
  and and_5 (and_5_out, Y_prime, C);
  and and_6 (and_6_out, X_prime, Z_prime);
  and and_7 (and_7_out, and_1_out, and_2_out);
  and and_8 (and_8_out, and_6_out, B);
  or or_14 (or_14_out, and_7_out, and_3_out);
  or or_15 (or_15_out, and_2_out, and_4_out);
  or or_16 (or_16_out, and_5_out, and_8_out);
  or or_17 (or_17_out, or_16_out, W);
  or or_18 (or_18_out, and_4_out, and_6_out);
  D_Flip_Flop d_ff_1 (.clk(clock_1_out), .D(or_14_out), .Q(W), .Qn(W_prime));  // open: preset, en, reset
  D_Flip_Flop d_ff_2 (.clk(clock_1_out), .D(or_15_out), .Q(A), .Qn(X_prime));  // open: preset, en, reset
  D_Flip_Flop d_ff_3 (.clk(clock_1_out), .D(or_17_out), .Q(B), .Qn(Y_prime));  // open: preset, en, reset
  D_Flip_Flop d_ff_4 (.clk(clock_1_out), .D(or_18_out), .Q(C), .Qn(Z_prime));  // open: preset, en, reset

  // Other names for the same wires on the sheet: Z = C; Y = B; X = A

  // Notes on the sheet:
  //   B
  //   C
  //   E
  //   F
  //   A
  //   D
  //   G
  //   W'
  //   X
  //   W
  //   Y
  //   X'
  //   Z'
  //   Y'
  //   Z
endmodule
